// Logisim project full-adder.circ as structural Verilog: 1 circuit, main circuit main
module main (
  input  A,
  input  B,
  input  Cin,
  output S,
  output Cout
);

  wire N1_out, N2_out, X1_out;

  xor X1 (X1_out, A, B);
  and N1 (N1_out, A, B);
  xor X2 (S, X1_out, Cin);
  and N2 (N2_out, X1_out, Cin);
  or O1 (Cout, N1_out, N2_out);
endmodule
