// Logisim project ripple-adder-4bit.circ as structural Verilog: 2 circuits, main circuit main
module main (
  input  Cin,
  input  A0,
  input  B0,
  input  A1,
  input  B1,
  input  A2,
  input  B2,
  input  A3,
  input  B3,
  output S0,
  output S1,
  output S2,
  output S3,
  output Cout
);

  wire U0_cout, U1_cout, U2_cout;

  FA U0 (.A(A0), .B(B0), .Cin(Cin), .S(S0), .Cout(U0_cout));
  FA U1 (.A(A1), .B(B1), .Cin(U0_cout), .S(S1), .Cout(U1_cout));
  FA U2 (.A(A2), .B(B2), .Cin(U1_cout), .S(S2), .Cout(U2_cout));
  FA U3 (.A(A3), .B(B3), .Cin(U2_cout), .S(S3), .Cout(Cout));
endmodule

module FA (
  input  A,
  input  B,
  input  Cin,
  output S,
  output Cout
);

  wire N1_out, N2_out, undriven, X1_out;

  xor X1 (X1_out, A, B);
  and N1 (N1_out, A, undriven);
  xor X2 (S, X1_out, Cin);
  and N2 (N2_out, X1_out, Cin);
  or O1 (Cout, N1_out, N2_out);
endmodule
